# Fritzing sketch WDI Fritzing (saved by Fritzing 0.9.3b)
perfboards: 2

parts:
  Power_plug1 = Power plug  # not connected
  U2 = Voltage Regulator - 5V [package="DPak [SMD]"]  # not connected
  U1 = NodeMCU V3.0
  Q1 = npn-Powertransistor [package="TO220 [THT]"]  # not connected
  Q2 = npn-Powertransistor [package="TO220 [THT]"]  # not connected
  Q4 = npn-Powertransistor [package="TO220 [THT]"]  # not connected
  R3 = Resistor [tolerance=±5% resistance=220 package="2512 [SMD]"]
  R4 = Resistor [tolerance=±5% resistance=220 package="2512 [SMD]"]
  R5 = Resistor [tolerance=±5% resistance=220 package="2512 [SMD]"]
  Q3 = npn-Powertransistor [package="TO220 [THT]"]  # not connected
  R1 = Resistor [tolerance=±5% resistance=220 package="2512 [SMD]"]
  U3 = NodeMCU V3.0
  Power_plug2 = Power plug  # not connected
  Q5 = npn-Powertransistor [package="TO220 [THT]"]  # not connected
  R6 = Resistor [tolerance=±5% resistance=220 package="2512 [SMD]"]
  Q6 = npn-Powertransistor [package="TO220 [THT]"]
  R7 = Resistor [tolerance=±5% resistance=220 package="2512 [SMD]"]
  Q7 = npn-Powertransistor [package="TO220 [THT]"]
  Q8 = npn-Powertransistor [package="TO220 [THT]"]
  R8 = Resistor [tolerance=±5% resistance=220 package="2512 [SMD]"]
  R9 = Resistor [tolerance=±5% resistance=220 package="2512 [SMD]"]
  U4 = Voltage Regulator - 5V [package="DPak [SMD]"]  # not connected

nets:
  N1: U1.D1, R4.Pin_1
  N2: U1.D2, R3.Pin_1
  N3: U1.GND#6, U1.GND#13, U1.GND#16, U1.GND#33
  N4: U1.D5, R5.Pin_1
  N5: U1.D6, R1.Pin_1
  N6: U3.D0, R9.Pin_1
  N7: U3.D2, R8.Pin_1
  N8: U3.GND#6, U3.GND#13, U3.GND#16, U3.GND#33
  N9: U3.D5, R7.Pin_1
  N10: U3.D8, R6.Pin_1
  N11: Q6.base, R7.Pin_0
  N12: Q7.base, R8.Pin_0
  N13: Q8.base, R9.Pin_0

custom parts:
  NodeMCU V3.0: ESP8266 based NodeMCU
